// Logisim project 32 Bit ALU.circ as structural Verilog: 11 circuits, main circuit main
module main (
  input  [31:0] Input1,
  input  [2:0] c,
  input  [31:0] Input2,
  output [31:0] Output
);

  wire [31:0] ADD_result, AND_result, divider_1_out, multiplier_1_out, n32_bit_subtractor_1_result,
       Negation_negation, NOT_result, OR_result;

  // Probe on Input2
  // Probe on Input1
  NOT_32_bit NOT (.A(Input1), .Result(NOT_result));
  _32_bit_OR OR (.A(Input1), .B(Input2), .Result(OR_result));
  _32_bit_AND AND (.A(Input2), .B(Input1), .Result(AND_result));
  Two_s_Complement_32_bit Negation (.A(Input1), .Negation(Negation_negation));
  _32_bit_Adder ADD (.A(Input2), .B(Input1), .Result(ADD_result));
  _32_bit_Subtractor u_32_bit_subtractor_1 (
    .A(Input1), .B(Input2), .Borrow_In(1'b0), .Result(n32_bit_subtractor_1_result));
  Multiplier #(.width(32)) multiplier_1 (.a(Input1), .b(Input2), .out(multiplier_1_out));  // open: cin, cout
  Divider #(.width(32)) divider_1 (.a(Input1), .b(Input2), .out(divider_1_out));  // open: upper, rem
  Multiplexer #(.select(3), .width(32), .enable("false")) multiplexer_1 (
    .in0(NOT_result), .in1(OR_result), .in2(AND_result), .in3(Negation_negation), .in4(ADD_result),
    .in5(n32_bit_subtractor_1_result), .in6(multiplier_1_out), .in7(divider_1_out), .out(Output), .sel(c));
  // Probe on Output

  // Notes on the sheet:
  //   Note:- The circuit of 32 bit multiplier is built as a sub-circuit but not added here due to clock and automation.
  //   Division
  //   32 BIT ALU
  //   Divya Prakash
  //   National Institute of Technology Patna
  //   Multiplication
  //   000: NOT
  //   001: OR
  //   010: AND
  //   011: Negation
  //   100: Addition
  //   101: Subtraction
  //   110: Multiplication
  //   111: Divisor
  //   Flags
endmodule

module _32_bit_Adder (
  input  [31:0] A,
  input  [31:0] B,
  output [31:0] Result
);

  wire full_adder_1_carry_out, full_adder_2_carry_out, full_adder_3_carry_out, full_adder_4_carry_out,
       full_adder_5_carry_out, full_adder_6_carry_out, full_adder_7_carry_out, full_adder_8_carry_out,
       full_adder_9_carry_out, full_adder_10_carry_out, full_adder_11_carry_out, full_adder_12_carry_out,
       full_adder_13_carry_out, full_adder_14_carry_out, full_adder_15_carry_out, full_adder_16_carry_out,
       full_adder_17_carry_out, full_adder_18_carry_out, full_adder_19_carry_out, full_adder_20_carry_out,
       full_adder_21_carry_out, full_adder_22_carry_out, full_adder_23_carry_out, full_adder_24_carry_out,
       full_adder_25_carry_out, full_adder_26_carry_out, full_adder_27_carry_out, full_adder_28_carry_out,
       full_adder_29_carry_out, full_adder_30_carry_out, full_adder_31_carry_out;

  Full_Adder full_adder_1 (
    .A(A[24]), .B(B[24]), .Carry_In(1'b0), .Result(Result[24]), .Carry_out(full_adder_1_carry_out));
  Full_Adder full_adder_2 (
    .A(A[25]), .B(B[25]), .Carry_In(full_adder_1_carry_out), .Result(Result[25]),
    .Carry_out(full_adder_2_carry_out));
  Full_Adder full_adder_3 (
    .A(A[26]), .B(B[26]), .Carry_In(full_adder_2_carry_out), .Result(Result[26]),
    .Carry_out(full_adder_3_carry_out));
  Full_Adder full_adder_4 (
    .A(A[27]), .B(B[27]), .Carry_In(full_adder_3_carry_out), .Result(Result[27]),
    .Carry_out(full_adder_4_carry_out));
  Full_Adder full_adder_5 (
    .A(A[28]), .B(B[28]), .Carry_In(full_adder_4_carry_out), .Result(Result[28]),
    .Carry_out(full_adder_5_carry_out));
  Full_Adder full_adder_6 (
    .A(A[29]), .B(B[29]), .Carry_In(full_adder_5_carry_out), .Result(Result[29]),
    .Carry_out(full_adder_6_carry_out));
  Full_Adder full_adder_7 (
    .A(A[30]), .B(B[30]), .Carry_In(full_adder_6_carry_out), .Result(Result[30]),
    .Carry_out(full_adder_7_carry_out));
  Full_Adder full_adder_8 (
    .A(A[31]), .B(B[31]), .Carry_In(full_adder_7_carry_out), .Result(Result[31]),
    .Carry_out(full_adder_8_carry_out));
  Full_Adder full_adder_9 (
    .A(A[16]), .B(B[16]), .Carry_In(full_adder_8_carry_out), .Result(Result[16]),
    .Carry_out(full_adder_9_carry_out));
  Full_Adder full_adder_10 (
    .A(A[17]), .B(B[17]), .Carry_In(full_adder_9_carry_out), .Result(Result[17]),
    .Carry_out(full_adder_10_carry_out));
  Full_Adder full_adder_11 (
    .A(A[18]), .B(B[18]), .Carry_In(full_adder_10_carry_out), .Result(Result[18]),
    .Carry_out(full_adder_11_carry_out));
  Full_Adder full_adder_12 (
    .A(A[19]), .B(B[19]), .Carry_In(full_adder_11_carry_out), .Result(Result[19]),
    .Carry_out(full_adder_12_carry_out));
  Full_Adder full_adder_13 (
    .A(A[20]), .B(B[20]), .Carry_In(full_adder_12_carry_out), .Result(Result[20]),
    .Carry_out(full_adder_13_carry_out));
  Full_Adder full_adder_14 (
    .A(A[21]), .B(B[21]), .Carry_In(full_adder_13_carry_out), .Result(Result[21]),
    .Carry_out(full_adder_14_carry_out));
  Full_Adder full_adder_15 (
    .A(A[22]), .B(B[22]), .Carry_In(full_adder_14_carry_out), .Result(Result[22]),
    .Carry_out(full_adder_15_carry_out));
  Full_Adder full_adder_16 (
    .A(A[23]), .B(B[23]), .Carry_In(full_adder_15_carry_out), .Result(Result[23]),
    .Carry_out(full_adder_16_carry_out));
  Full_Adder full_adder_17 (
    .A(A[8]), .B(B[8]), .Carry_In(full_adder_16_carry_out), .Result(Result[8]),
    .Carry_out(full_adder_17_carry_out));
  Full_Adder full_adder_18 (
    .A(A[9]), .B(B[9]), .Carry_In(full_adder_17_carry_out), .Result(Result[9]),
    .Carry_out(full_adder_18_carry_out));
  Full_Adder full_adder_19 (
    .A(A[10]), .B(B[10]), .Carry_In(full_adder_18_carry_out), .Result(Result[10]),
    .Carry_out(full_adder_19_carry_out));
  Full_Adder full_adder_20 (
    .A(A[11]), .B(B[11]), .Carry_In(full_adder_19_carry_out), .Result(Result[11]),
    .Carry_out(full_adder_20_carry_out));
  Full_Adder full_adder_21 (
    .A(A[12]), .B(B[12]), .Carry_In(full_adder_20_carry_out), .Result(Result[12]),
    .Carry_out(full_adder_21_carry_out));
  Full_Adder full_adder_22 (
    .A(A[13]), .B(B[13]), .Carry_In(full_adder_21_carry_out), .Result(Result[13]),
    .Carry_out(full_adder_22_carry_out));
  Full_Adder full_adder_23 (
    .A(A[14]), .B(B[14]), .Carry_In(full_adder_22_carry_out), .Result(Result[14]),
    .Carry_out(full_adder_23_carry_out));
  Full_Adder full_adder_24 (
    .A(A[15]), .B(B[15]), .Carry_In(full_adder_23_carry_out), .Result(Result[15]),
    .Carry_out(full_adder_24_carry_out));
  Full_Adder full_adder_25 (
    .A(A[0]), .B(B[0]), .Carry_In(full_adder_24_carry_out), .Result(Result[0]),
    .Carry_out(full_adder_25_carry_out));
  Full_Adder full_adder_26 (
    .A(A[1]), .B(B[1]), .Carry_In(full_adder_25_carry_out), .Result(Result[1]),
    .Carry_out(full_adder_26_carry_out));
  Full_Adder full_adder_27 (
    .A(A[2]), .B(B[2]), .Carry_In(full_adder_26_carry_out), .Result(Result[2]),
    .Carry_out(full_adder_27_carry_out));
  Full_Adder full_adder_28 (
    .A(A[3]), .B(B[3]), .Carry_In(full_adder_27_carry_out), .Result(Result[3]),
    .Carry_out(full_adder_28_carry_out));
  Full_Adder full_adder_29 (
    .A(A[4]), .B(B[4]), .Carry_In(full_adder_28_carry_out), .Result(Result[4]),
    .Carry_out(full_adder_29_carry_out));
  Full_Adder full_adder_30 (
    .A(A[5]), .B(B[5]), .Carry_In(full_adder_29_carry_out), .Result(Result[5]),
    .Carry_out(full_adder_30_carry_out));
  Full_Adder full_adder_31 (
    .A(A[6]), .B(B[6]), .Carry_In(full_adder_30_carry_out), .Result(Result[6]),
    .Carry_out(full_adder_31_carry_out));
  Full_Adder full_adder_32 (
    .A(A[7]), .B(B[7]), .Carry_In(full_adder_31_carry_out), .Result(Result[7]));  // open: Carry_out
endmodule

module _32_bit_AND (
  input  [31:0] A,
  input  [31:0] B,
  output [31:0] Result
);

  and and_1 (Result[24], A[24], B[24]);
  and and_2 (Result[25], A[25], B[25]);
  and and_3 (Result[26], A[26], B[26]);
  and and_4 (Result[27], A[27], B[27]);
  and and_5 (Result[28], A[28], B[28]);
  and and_6 (Result[29], A[29], B[29]);
  and and_7 (Result[30], A[30], B[30]);
  and and_8 (Result[31], A[31], B[31]);
  and and_9 (Result[16], A[16], B[16]);
  and and_10 (Result[17], A[17], B[17]);
  and and_11 (Result[18], A[18], B[18]);
  and and_12 (Result[19], A[19], B[19]);
  and and_13 (Result[20], A[20], B[20]);
  and and_14 (Result[21], A[21], B[21]);
  and and_15 (Result[22], A[22], B[22]);
  and and_16 (Result[23], A[23], B[23]);
  and and_17 (Result[8], A[8], B[8]);
  and and_18 (Result[9], A[9], B[9]);
  and and_19 (Result[10], A[10], B[10]);
  and and_20 (Result[11], A[11], B[11]);
  and and_21 (Result[12], A[12], B[12]);
  and and_22 (Result[13], A[13], B[13]);
  and and_23 (Result[14], A[14], B[14]);
  and and_24 (Result[15], A[15], B[15]);
  and and_25 (Result[0], A[0], B[0]);
  and and_26 (Result[1], A[1], B[1]);
  and and_27 (Result[2], A[2], B[2]);
  and and_28 (Result[3], A[3], B[3]);
  and and_29 (Result[4], A[4], B[4]);
  buf and_30 (Result[5], A[5]);  // AND_Gate
  buf and_31 (Result[6], A[6]);  // AND_Gate
  and and_32 (Result[7], A[7], B[7]);
endmodule

module _32_bit_OR (
  input  [31:0] A,
  input  [31:0] B,
  output [31:0] Result
);

  or or_1 (Result[24], A[24], B[24]);
  or or_2 (Result[25], A[25], B[25]);
  or or_3 (Result[26], A[26], B[26]);
  or or_4 (Result[27], A[27], B[27]);
  or or_5 (Result[28], A[28], B[28]);
  or or_6 (Result[29], A[29], B[29]);
  or or_7 (Result[30], A[30], B[30]);
  or or_8 (Result[31], A[31], B[31]);
  or or_9 (Result[16], A[16], B[16]);
  or or_10 (Result[17], A[17], B[17]);
  or or_11 (Result[18], A[18], B[18]);
  or or_12 (Result[19], A[19], B[19]);
  or or_13 (Result[20], A[20], B[20]);
  or or_14 (Result[21], A[21], B[21]);
  or or_15 (Result[22], A[22], B[22]);
  or or_16 (Result[23], A[23], B[23]);
  or or_17 (Result[8], A[8], B[8]);
  or or_18 (Result[9], A[9], B[9]);
  or or_19 (Result[10], A[10], B[10]);
  or or_20 (Result[11], A[11], B[11]);
  or or_21 (Result[12], A[12], B[12]);
  or or_22 (Result[13], A[13], B[13]);
  or or_23 (Result[14], A[14], B[14]);
  or or_24 (Result[15], A[15], B[15]);
  or or_25 (Result[0], A[0], B[0]);
  or or_26 (Result[1], A[1], B[1]);
  or or_27 (Result[2], A[2], B[2]);
  or or_28 (Result[3], A[3], B[3]);
  or or_29 (Result[4], A[4], B[4]);
  or or_30 (Result[5], A[5], B[5]);
  or or_31 (Result[6], A[6], B[6]);
  or or_32 (Result[7], A[7], B[7]);
endmodule

module _32_bit_Subtractor (
  input  [31:0] A,
  input  Borrow_In,
  input  [31:0] B,
  output [31:0] Result
);

  wire full_subtractor_1_borrow_out, full_subtractor_2_borrow_out, full_subtractor_3_borrow_out,
       full_subtractor_4_borrow_out, full_subtractor_5_borrow_out, full_subtractor_6_borrow_out,
       full_subtractor_7_borrow_out, full_subtractor_8_borrow_out, full_subtractor_9_borrow_out,
       full_subtractor_10_borrow_out, full_subtractor_11_borrow_out, full_subtractor_12_borrow_out,
       full_subtractor_13_borrow_out, full_subtractor_14_borrow_out, full_subtractor_15_borrow_out,
       full_subtractor_16_borrow_out, full_subtractor_17_borrow_out, full_subtractor_18_borrow_out,
       full_subtractor_19_borrow_out, full_subtractor_20_borrow_out, full_subtractor_21_borrow_out,
       full_subtractor_22_borrow_out, full_subtractor_23_borrow_out, full_subtractor_24_borrow_out,
       full_subtractor_25_borrow_out, full_subtractor_26_borrow_out, full_subtractor_27_borrow_out,
       full_subtractor_28_borrow_out, full_subtractor_29_borrow_out, full_subtractor_30_borrow_out,
       full_subtractor_31_borrow_out;

  Full_Subtractor full_subtractor_1 (
    .A(A[24]), .B(B[24]), .Borrow_in(Borrow_In), .Difference(Result[24]),
    .Borrow_out(full_subtractor_1_borrow_out));
  Full_Subtractor full_subtractor_2 (
    .A(A[25]), .B(B[25]), .Borrow_in(full_subtractor_1_borrow_out), .Difference(Result[25]),
    .Borrow_out(full_subtractor_2_borrow_out));
  Full_Subtractor full_subtractor_3 (
    .A(A[26]), .B(B[26]), .Borrow_in(full_subtractor_2_borrow_out), .Difference(Result[26]),
    .Borrow_out(full_subtractor_3_borrow_out));
  Full_Subtractor full_subtractor_4 (
    .A(A[27]), .B(B[27]), .Borrow_in(full_subtractor_3_borrow_out), .Difference(Result[27]),
    .Borrow_out(full_subtractor_4_borrow_out));
  Full_Subtractor full_subtractor_5 (
    .A(A[28]), .B(B[28]), .Borrow_in(full_subtractor_4_borrow_out), .Difference(Result[28]),
    .Borrow_out(full_subtractor_5_borrow_out));
  Full_Subtractor full_subtractor_6 (
    .A(A[29]), .B(B[29]), .Borrow_in(full_subtractor_5_borrow_out), .Difference(Result[29]),
    .Borrow_out(full_subtractor_6_borrow_out));
  Full_Subtractor full_subtractor_7 (
    .A(A[30]), .B(B[30]), .Borrow_in(full_subtractor_6_borrow_out), .Difference(Result[30]),
    .Borrow_out(full_subtractor_7_borrow_out));
  Full_Subtractor full_subtractor_8 (
    .A(A[31]), .B(B[31]), .Borrow_in(full_subtractor_7_borrow_out), .Difference(Result[31]),
    .Borrow_out(full_subtractor_8_borrow_out));
  Full_Subtractor full_subtractor_9 (
    .A(A[16]), .B(B[16]), .Borrow_in(full_subtractor_8_borrow_out), .Difference(Result[16]),
    .Borrow_out(full_subtractor_9_borrow_out));
  Full_Subtractor full_subtractor_10 (
    .A(A[17]), .B(B[17]), .Borrow_in(full_subtractor_9_borrow_out), .Difference(Result[17]),
    .Borrow_out(full_subtractor_10_borrow_out));
  Full_Subtractor full_subtractor_11 (
    .A(A[18]), .B(B[18]), .Borrow_in(full_subtractor_10_borrow_out), .Difference(Result[18]),
    .Borrow_out(full_subtractor_11_borrow_out));
  Full_Subtractor full_subtractor_12 (
    .A(A[19]), .B(B[19]), .Borrow_in(full_subtractor_11_borrow_out), .Difference(Result[19]),
    .Borrow_out(full_subtractor_12_borrow_out));
  Full_Subtractor full_subtractor_13 (
    .A(A[20]), .B(B[20]), .Borrow_in(full_subtractor_12_borrow_out), .Difference(Result[20]),
    .Borrow_out(full_subtractor_13_borrow_out));
  Full_Subtractor full_subtractor_14 (
    .A(A[21]), .B(B[21]), .Borrow_in(full_subtractor_13_borrow_out), .Difference(Result[21]),
    .Borrow_out(full_subtractor_14_borrow_out));
  Full_Subtractor full_subtractor_15 (
    .A(A[22]), .B(B[22]), .Borrow_in(full_subtractor_14_borrow_out), .Difference(Result[22]),
    .Borrow_out(full_subtractor_15_borrow_out));
  Full_Subtractor full_subtractor_16 (
    .A(A[23]), .B(B[23]), .Borrow_in(full_subtractor_15_borrow_out), .Difference(Result[23]),
    .Borrow_out(full_subtractor_16_borrow_out));
  Full_Subtractor full_subtractor_17 (
    .A(A[8]), .B(B[8]), .Borrow_in(full_subtractor_16_borrow_out), .Difference(Result[8]),
    .Borrow_out(full_subtractor_17_borrow_out));
  Full_Subtractor full_subtractor_18 (
    .A(A[9]), .B(B[9]), .Borrow_in(full_subtractor_17_borrow_out), .Difference(Result[9]),
    .Borrow_out(full_subtractor_18_borrow_out));
  Full_Subtractor full_subtractor_19 (
    .A(A[10]), .B(B[10]), .Borrow_in(full_subtractor_18_borrow_out), .Difference(Result[10]),
    .Borrow_out(full_subtractor_19_borrow_out));
  Full_Subtractor full_subtractor_20 (
    .A(A[11]), .B(B[11]), .Borrow_in(full_subtractor_19_borrow_out), .Difference(Result[11]),
    .Borrow_out(full_subtractor_20_borrow_out));
  Full_Subtractor full_subtractor_21 (
    .A(A[12]), .B(B[12]), .Borrow_in(full_subtractor_20_borrow_out), .Difference(Result[12]),
    .Borrow_out(full_subtractor_21_borrow_out));
  Full_Subtractor full_subtractor_22 (
    .A(A[13]), .B(B[13]), .Borrow_in(full_subtractor_21_borrow_out), .Difference(Result[13]),
    .Borrow_out(full_subtractor_22_borrow_out));
  Full_Subtractor full_subtractor_23 (
    .A(A[14]), .B(B[14]), .Borrow_in(full_subtractor_22_borrow_out), .Difference(Result[14]),
    .Borrow_out(full_subtractor_23_borrow_out));
  Full_Subtractor full_subtractor_24 (
    .A(A[15]), .B(B[15]), .Borrow_in(full_subtractor_23_borrow_out), .Difference(Result[15]),
    .Borrow_out(full_subtractor_24_borrow_out));
  Full_Subtractor full_subtractor_25 (
    .A(A[0]), .B(B[0]), .Borrow_in(full_subtractor_24_borrow_out), .Difference(Result[0]),
    .Borrow_out(full_subtractor_25_borrow_out));
  Full_Subtractor full_subtractor_26 (
    .A(A[1]), .B(B[1]), .Borrow_in(full_subtractor_25_borrow_out), .Difference(Result[1]),
    .Borrow_out(full_subtractor_26_borrow_out));
  Full_Subtractor full_subtractor_27 (
    .A(A[2]), .B(B[2]), .Borrow_in(full_subtractor_26_borrow_out), .Difference(Result[2]),
    .Borrow_out(full_subtractor_27_borrow_out));
  Full_Subtractor full_subtractor_28 (
    .A(A[3]), .B(B[3]), .Borrow_in(full_subtractor_27_borrow_out), .Difference(Result[3]),
    .Borrow_out(full_subtractor_28_borrow_out));
  Full_Subtractor full_subtractor_29 (
    .A(A[4]), .B(B[4]), .Borrow_in(full_subtractor_28_borrow_out), .Difference(Result[4]),
    .Borrow_out(full_subtractor_29_borrow_out));
  Full_Subtractor full_subtractor_30 (
    .A(A[5]), .B(B[5]), .Borrow_in(full_subtractor_29_borrow_out), .Difference(Result[5]),
    .Borrow_out(full_subtractor_30_borrow_out));
  Full_Subtractor full_subtractor_31 (
    .A(A[6]), .B(B[6]), .Borrow_in(full_subtractor_30_borrow_out), .Difference(Result[6]),
    .Borrow_out(full_subtractor_31_borrow_out));
  Full_Subtractor full_subtractor_32 (
    .A(A[7]), .B(B[7]), .Borrow_in(full_subtractor_31_borrow_out), .Difference(Result[7]));  // open: Borrow_out
endmodule

module Full_Adder (
  input  Carry_In,
  input  A,
  input  B,
  output Result,
  output Carry_out
);

  wire and_1_out, and_2_out, xor_1_out;

  xor xor_1 (xor_1_out, A, B);
  and and_1 (and_1_out, B, A);
  and and_2 (and_2_out, xor_1_out, Carry_In);
  xor xor_2 (Result, Carry_In, xor_1_out);
  or or_1 (Carry_out, and_2_out, and_1_out);
endmodule

module NOT_32_bit (
  input  [31:0] A,
  output [31:0] Result
);

  not not_1 (Result[24], A[24]);
  not not_2 (Result[25], A[25]);
  not not_3 (Result[26], A[26]);
  not not_4 (Result[27], A[27]);
  not not_5 (Result[28], A[28]);
  not not_6 (Result[29], A[29]);
  not not_7 (Result[30], A[30]);
  not not_8 (Result[31], A[31]);
  not not_9 (Result[16], A[16]);
  not not_10 (Result[17], A[17]);
  not not_11 (Result[18], A[18]);
  not not_12 (Result[19], A[19]);
  not not_13 (Result[20], A[20]);
  not not_14 (Result[21], A[21]);
  not not_15 (Result[22], A[22]);
  not not_16 (Result[23], A[23]);
  not not_17 (Result[8], A[8]);
  not not_18 (Result[9], A[9]);
  not not_19 (Result[10], A[10]);
  not not_20 (Result[11], A[11]);
  not not_21 (Result[12], A[12]);
  not not_22 (Result[13], A[13]);
  not not_23 (Result[14], A[14]);
  not not_24 (Result[15], A[15]);
  not not_25 (Result[0], A[0]);
  not not_26 (Result[1], A[1]);
  not not_27 (Result[2], A[2]);
  not not_28 (Result[3], A[3]);
  not not_29 (Result[4], A[4]);
  not not_30 (Result[5], A[5]);
  not not_31 (Result[6], A[6]);
  not not_32 (Result[7], A[7]);
endmodule

module Two_s_Complement_32_bit (
  input  [31:0] A,
  output [31:0] Negation
);

  wire [31:0] not_32_bit_1_result;

  NOT_32_bit not_32_bit_1 (.A(A), .Result(not_32_bit_1_result));
  _32_bit_Adder u_32_bit_adder_1 (.A(not_32_bit_1_result), .B({32{1'b0}}), .Result(Negation));
endmodule

module _32_bit_multiplier (
  input  [31:0] M,
  input  [31:0] Q,
  input  Init,
  output out_4,
  output out_5,
  output [31:0] MSB,
  output [31:0] LSB
);

  wire and_2_out, Clk_out, counter_1_carry, not_2_out, not_3_out, shift_register_1_out, shift_register_2_out,
       shift_register_3_q0, xnor_1_out;
  wire [31:0] multiplexer_3_out, n32_bit_subtractor_1_result, shift_register_1_q31, shift_register_2_q31;

  Clock Clk (.out(Clk_out));
  not not_1 (out_4, counter_1_carry);
  and and_1 (out_5, Clk_out, out_4);
  not not_2 (not_2_out, out_5);
  Counter #(.width(6), .max('h3f), .ongoal("stay")) counter_1 (
    .carry(counter_1_carry), .clk(out_5));  // open: load, D, count, Q, clr
  Shift_Register #(.length(32)) shift_register_1 (
    .shift(not_2_out), .in(shift_register_1_q31[31]), .clk(out_5), .out(shift_register_1_out), .load(out_5),
    .d0(multiplexer_3_out[31]), .q0(shift_register_1_q31[31]), .d1(multiplexer_3_out[30]),
    .q1(shift_register_1_q31[30]), .d2(multiplexer_3_out[29]), .q2(shift_register_1_q31[29]),
    .d3(multiplexer_3_out[28]), .q3(shift_register_1_q31[28]), .d4(multiplexer_3_out[27]),
    .q4(shift_register_1_q31[27]), .d5(multiplexer_3_out[26]), .q5(shift_register_1_q31[26]),
    .d6(multiplexer_3_out[25]), .q6(shift_register_1_q31[25]), .d7(multiplexer_3_out[24]),
    .q7(shift_register_1_q31[24]), .d8(multiplexer_3_out[23]), .q8(shift_register_1_q31[23]),
    .d9(multiplexer_3_out[22]), .q9(shift_register_1_q31[22]), .d10(multiplexer_3_out[21]),
    .q10(shift_register_1_q31[21]), .d11(multiplexer_3_out[20]), .q11(shift_register_1_q31[20]),
    .d12(multiplexer_3_out[19]), .q12(shift_register_1_q31[19]), .d13(multiplexer_3_out[18]),
    .q13(shift_register_1_q31[18]), .d14(multiplexer_3_out[17]), .q14(shift_register_1_q31[17]),
    .d15(multiplexer_3_out[16]), .q15(shift_register_1_q31[16]), .d16(multiplexer_3_out[15]),
    .q16(shift_register_1_q31[15]), .d17(multiplexer_3_out[14]), .q17(shift_register_1_q31[14]),
    .d18(multiplexer_3_out[13]), .q18(shift_register_1_q31[13]), .d19(multiplexer_3_out[12]),
    .q19(shift_register_1_q31[12]), .d20(multiplexer_3_out[11]), .q20(shift_register_1_q31[11]),
    .d21(multiplexer_3_out[10]), .q21(shift_register_1_q31[10]), .d22(multiplexer_3_out[9]),
    .q22(shift_register_1_q31[9]), .d23(multiplexer_3_out[8]), .q23(shift_register_1_q31[8]),
    .d24(multiplexer_3_out[7]), .q24(shift_register_1_q31[7]), .d25(multiplexer_3_out[6]),
    .q25(shift_register_1_q31[6]), .d26(multiplexer_3_out[5]), .q26(shift_register_1_q31[5]),
    .d27(multiplexer_3_out[4]), .q27(shift_register_1_q31[4]), .d28(multiplexer_3_out[3]),
    .q28(shift_register_1_q31[3]), .d29(multiplexer_3_out[2]), .q29(shift_register_1_q31[2]),
    .d30(multiplexer_3_out[1]), .q30(shift_register_1_q31[1]), .d31(multiplexer_3_out[0]),
    .q31(shift_register_1_q31[0]));  // open: clr
  Multiplexer #(.width(32), .enable("false")) multiplexer_1 (
    .in0({32{1'b0}}), .in1(shift_register_1_q31), .out(MSB), .sel(counter_1_carry));
  Multiplexer #(.width(32), .enable("false")) multiplexer_2 (
    .in0({32{1'b0}}), .in1(shift_register_2_q31), .out(LSB), .sel(counter_1_carry));
  Shift_Register #(.length(32)) shift_register_2 (
    .shift(not_2_out), .in(shift_register_1_out), .clk(out_5), .out(shift_register_2_out), .load(Init),
    .d0(Q[31]), .q0(shift_register_2_q31[31]), .d1(Q[30]), .q1(shift_register_2_q31[30]), .d2(Q[29]),
    .q2(shift_register_2_q31[29]), .d3(Q[28]), .q3(shift_register_2_q31[28]), .d4(Q[27]),
    .q4(shift_register_2_q31[27]), .d5(Q[26]), .q5(shift_register_2_q31[26]), .d6(Q[25]),
    .q6(shift_register_2_q31[25]), .d7(Q[24]), .q7(shift_register_2_q31[24]), .d8(Q[23]),
    .q8(shift_register_2_q31[23]), .d9(Q[22]), .q9(shift_register_2_q31[22]), .d10(Q[21]),
    .q10(shift_register_2_q31[21]), .d11(Q[20]), .q11(shift_register_2_q31[20]), .d12(Q[19]),
    .q12(shift_register_2_q31[19]), .d13(Q[18]), .q13(shift_register_2_q31[18]), .d14(Q[17]),
    .q14(shift_register_2_q31[17]), .d15(Q[16]), .q15(shift_register_2_q31[16]), .d16(Q[15]),
    .q16(shift_register_2_q31[15]), .d17(Q[14]), .q17(shift_register_2_q31[14]), .d18(Q[13]),
    .q18(shift_register_2_q31[13]), .d19(Q[12]), .q19(shift_register_2_q31[12]), .d20(Q[11]),
    .q20(shift_register_2_q31[11]), .d21(Q[10]), .q21(shift_register_2_q31[10]), .d22(Q[9]),
    .q22(shift_register_2_q31[9]), .d23(Q[8]), .q23(shift_register_2_q31[8]), .d24(Q[7]),
    .q24(shift_register_2_q31[7]), .d25(Q[6]), .q25(shift_register_2_q31[6]), .d26(Q[5]),
    .q26(shift_register_2_q31[5]), .d27(Q[4]), .q27(shift_register_2_q31[4]), .d28(Q[3]),
    .q28(shift_register_2_q31[3]), .d29(Q[2]), .q29(shift_register_2_q31[2]), .d30(Q[1]),
    .q30(shift_register_2_q31[1]), .d31(Q[0]), .q31(shift_register_2_q31[0]));  // open: clr
  Multiplexer #(.width(32), .enable("false")) multiplexer_3 (
    .in0(n32_bit_subtractor_1_result), .in1(shift_register_1_q31), .out(multiplexer_3_out), .sel(xnor_1_out));
  _32_bit_Subtractor u_32_bit_subtractor_1 (
    .A(M), .B(shift_register_1_q31), .Borrow_In(and_2_out), .Result(n32_bit_subtractor_1_result));
  xnor xnor_1 (xnor_1_out, shift_register_2_q31[0], shift_register_3_q0);
  and and_2 (and_2_out, shift_register_2_q31[0], not_3_out);
  not not_3 (not_3_out, shift_register_3_q0);
  Shift_Register #(.length(1)) shift_register_3 (
    .shift(not_2_out), .in(shift_register_2_out), .clk(out_5), .q0(shift_register_3_q0));  // open: out, load, clr, d0
endmodule

module _4_bit_booth_multiplier (
  input  [3:0] M,
  input  [3:0] Q,
  input  Init,
  input  Shift,
  input  Load
);

  wire clock_1_out, shift_register_1_out, shift_register_2_out, shift_register_2_q3, shift_register_3_q0;
  wire [2:0] comparator_1_gt;
  wire [3:0] adder_1_out, multiplexer_1_out, shift_register_1_q3, subtractor_1_out;

  Multiplexer #(.select(3), .width(4)) multiplexer_1 (
    .in1(subtractor_1_out), .in2(shift_register_1_q3), .in4(adder_1_out), .out(multiplexer_1_out),
    .sel(comparator_1_gt));  // open: in0, in3, in5, in6, in7, en
  Clock clock_1 (.out(clock_1_out));
  Shift_Register #(.length(4)) shift_register_1 (
    .shift(Shift), .in(shift_register_1_q3[3]), .clk(clock_1_out), .out(shift_register_1_out), .load(Load),
    .d0(multiplexer_1_out[3]), .q0(shift_register_1_q3[3]), .d1(multiplexer_1_out[2]),
    .q1(shift_register_1_q3[2]), .d2(multiplexer_1_out[1]), .q2(shift_register_1_q3[1]),
    .d3(multiplexer_1_out[0]), .q3(shift_register_1_q3[0]));  // open: clr
  Shift_Register #(.length(4)) shift_register_2 (
    .shift(Shift), .in(shift_register_1_out), .clk(clock_1_out), .out(shift_register_2_out), .load(Init),
    .d0(Q[3]), .d1(Q[2]), .d2(Q[1]), .d3(Q[0]), .q3(shift_register_2_q3));  // open: clr, q0, q1, q2
  Subtractor #(.width(4)) subtractor_1 (
    .a(shift_register_1_q3), .b(M), .out(subtractor_1_out), .bin(1'b0));  // open: bout
  Adder #(.width(4)) adder_1 (.a(shift_register_1_q3), .b(M), .out(adder_1_out), .cin(1'b0));  // open: cout
  Shift_Register #(.length(1)) shift_register_3 (
    .shift(Shift), .in(shift_register_2_out), .clk(clock_1_out), .q0(shift_register_3_q0));  // open: out, load, clr, d0
  Comparator #(.width(1)) comparator_1 (
    .a(shift_register_3_q0), .b(shift_register_2_q3), .gt(comparator_1_gt[0]), .eq(comparator_1_gt[1]),
    .lt(comparator_1_gt[2]));
endmodule

module Full_Subtractor (
  input  Borrow_in,
  input  A,
  input  B,
  output Difference,
  output Borrow_out
);

  wire and_1_out, and_2_out, not_1_out, not_2_out, xor_1_out;

  not not_1 (not_1_out, A);
  xor xor_1 (xor_1_out, A, B);
  and and_1 (and_1_out, B, not_1_out);
  not not_2 (not_2_out, xor_1_out);
  and and_2 (and_2_out, not_2_out, Borrow_in);
  xor xor_2 (Difference, Borrow_in, xor_1_out);
  or or_1 (Borrow_out, and_2_out, and_1_out);
endmodule
